# Fritzing sketch V1_NW_MySensors (saved by Fritzing 0.9.3b)
breadboards: 1

parts:
  HLK-PM1 = HLK-PM01
  U1 = LMZ14203 [package=to-pmod-7]
  Onderdeel1 = Arduino Pro Mini (3.3V)
  Onderdeel2 = Adafruit 4-channel I2C-safe Bi-directional Logic Level Converter [part_number="Adafruit #757"]  # not connected

nets:
  GND: HLK-PM1.-Vo, U1.GND, Onderdeel1.GND
  N1: HLK-PM1.+Vo, U1.VIN
  N2: U1.VOUT, Onderdeel1.VCC

custom parts:
  Adafruit 4-channel I2C-safe Bi-directional Logic Level Converter: Because the Arduino (and Basic Stamp) are 5V devices, and most modern sensors, displays, flash cards and modes are 3.3V-only, many makers find that they need to perform level shifting/conversion to protect the 3.3V device from 5V. We do have some other handy level shifters in the shop, from the DIP 74LVC245 to the fancy bi-directional TXB0108. However, neither of these are happy to work with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
