# Fritzing sketch V1_NW_MySensors_RPi (saved by Fritzing 0.9.3b)

parts:
  Raspberry_Pi1 = Raspberry Pi 2
  RFM1 = RFM69HCW ISM Transciever
  U1 = RF-LINK_RX [package=rf-link_rx]  # not connected
  U2 = attiny85 [package=dip]  # not connected

nets:
  N1: Raspberry_Pi1.3V3, RFM1.13_3.3V
  N2: Raspberry_Pi1.GIPO10, RFM1.3_MOSI
  N3: Raspberry_Pi1.GIPO9, RFM1.2_MISO
  N4: Raspberry_Pi1.GIPO11, RFM1.4_SCK
  N5: Raspberry_Pi1.GIPO8, RFM1.5_NSS_(CS)
  N6: Raspberry_Pi1.GIPO25, RFM1.14_DIO0
  N7: Raspberry_Pi1.GND, RFM1.1_GND

custom parts:
  RFM69HCW ISM Transciever: RF Transceiver by Hope RF. Well supported Arduino libraries are available. This ISM band transceiver is available in several frequencies e.g. 433MHz and 915MHz and it is also available in various feature versions.
